// Logisim project computer_clark.circ as structural Verilog
module mem_bit (
  input  in_1,
  input  in_2,
  output out_3
);

  wire nand_transistores_1_out_3, nand_transistores_2_2_out_3, nand_transistores_2_out_3;

  nand_transistores nand_transistores_1 (.in_1(in_1), .in_2(in_2), .out_3(nand_transistores_1_out_3));
  nand_transistores nand_transistores_2 (
    .in_1(nand_transistores_1_out_3), .in_2(in_2), .out_3(nand_transistores_2_out_3));
  nand_transistores_2 nand_transistores_2_1 (
    .in_1(nand_transistores_1_out_3), .in_2(nand_transistores_2_2_out_3), .out_3(out_3));
  nand_transistores_2 nand_transistores_2_2 (
    .in_1(out_3), .in_2(nand_transistores_2_out_3), .out_3(nand_transistores_2_2_out_3));
endmodule

module mem_byte (
  input  in_1,
  input  in_2,
  input  in_3,
  input  in_4,
  input  in_5,
  input  in_6,
  input  in_7,
  input  in_8,
  input  in_9,
  output out_10,
  output out_11,
  output out_12,
  output out_13,
  output out_14,
  output out_15,
  output out_16,
  output out_17
);

  mem_bit mem_bit_1 (.in_1(in_1), .in_2(in_9), .out_3(out_10));
  mem_bit mem_bit_2 (.in_1(in_2), .in_2(in_9), .out_3(out_11));
  mem_bit mem_bit_3 (.in_1(in_3), .in_2(in_9), .out_3(out_12));
  mem_bit mem_bit_4 (.in_1(in_4), .in_2(in_9), .out_3(out_13));
  mem_bit mem_bit_5 (.in_1(in_5), .in_2(in_9), .out_3(out_14));
  mem_bit mem_bit_6 (.in_1(in_6), .in_2(in_9), .out_3(out_15));
  mem_bit mem_bit_7 (.in_1(in_7), .in_2(in_9), .out_3(out_16));
  mem_bit mem_bit_8 (.in_1(in_8), .in_2(in_9), .out_3(out_17));

  // Notes on the sheet:
  //   input
  //   set
  //   output
endmodule

module prueba_mem_byte (
  input  in_1,
  input  in_2,
  input  in_3,
  input  in_4,
  input  in_5,
  output out_6
);

  wire dipswitch_1_p1, dipswitch_1_p2, dipswitch_1_p3, dipswitch_1_p4, dipswitch_1_p5, dipswitch_1_p6,
       dipswitch_1_p7, dipswitch_1_p8, mem_bit_1_out_3, mem_byte_1_out_10, mem_byte_1_out_11,
       mem_byte_1_out_12, mem_byte_1_out_13, mem_byte_1_out_14, mem_byte_1_out_15, mem_byte_1_out_16,
       mem_byte_1_out_17;

  mem_bit mem_bit_1 (.in_1(in_1), .in_2(in_2), .out_3(mem_bit_1_out_3));
  LED led_1 (.in(mem_bit_1_out_3));
  // DipSwitch dipswitch_1: pin names not known; wires that end beside it: dipswitch_1_p1, dipswitch_1_p2, dipswitch_1_p3, dipswitch_1_p4, dipswitch_1_p5, dipswitch_1_p6, dipswitch_1_p7, dipswitch_1_p8
  nand_transistores nand_transistores_1 (.in_1(in_4), .in_2(in_5), .out_3(out_6));
  mem_byte mem_byte_1 (
    .in_2(dipswitch_1_p2), .in_3(dipswitch_1_p3), .in_4(dipswitch_1_p4), .in_5(dipswitch_1_p5),
    .in_6(dipswitch_1_p6), .in_7(dipswitch_1_p7), .in_8(dipswitch_1_p8), .in_1(dipswitch_1_p1), .in_9(in_3),
    .out_11(mem_byte_1_out_11), .out_12(mem_byte_1_out_12), .out_13(mem_byte_1_out_13),
    .out_14(mem_byte_1_out_14), .out_15(mem_byte_1_out_15), .out_16(mem_byte_1_out_16),
    .out_17(mem_byte_1_out_17), .out_10(mem_byte_1_out_10));
  LedBar ledbar_1 (
    .led0(mem_byte_1_out_10), .led1(mem_byte_1_out_11), .led2(mem_byte_1_out_12), .led3(mem_byte_1_out_13),
    .led4(mem_byte_1_out_14), .led5(mem_byte_1_out_15), .led6(mem_byte_1_out_16), .led7(mem_byte_1_out_17));

  // Notes on the sheet:
  //   Memoria de 1 bit
  //   Puerta NAND con transistores
  //   Memoria de 1 byte
endmodule

module nand_transistores (
  input  in_1,
  input  in_2,
  output out_3
);

  wire transistor_4_out;

  Transistor transistor_1 (.in(1'b1), .out(out_3), .gate(in_1));
  Transistor #(.\type ("n")) transistor_2 (.in(transistor_4_out), .out(out_3), .gate(in_1));
  Transistor transistor_3 (.in(1'b1), .out(out_3), .gate(in_2));
  Transistor #(.\type ("n")) transistor_4 (.in(1'b0), .out(transistor_4_out), .gate(in_2));
endmodule

module nand_transistores_2 (
  input  in_1,
  input  in_2,
  output out_3
);

  Transistor transistor_1 (.in(1'b1), .out(out_3), .gate(in_1));
  Transistor transistor_2 (.in(1'b1), .out(out_3), .gate(in_2));
  Pull_Resistor pull_resistor_1 (.node(out_3));

  // Notes on the sheet:
  //   in_1: pull=up
  //   in_2: pull=up
  //   out_3: pull=down
endmodule

module buffer_trans (
  input  in_1,
  output out_2
);

  wire transistor_1_out;

  Transistor transistor_1 (.in(1'b1), .out(transistor_1_out), .gate(in_1));
  Transistor #(.\type ("n")) transistor_2 (.in(1'b0), .out(transistor_1_out), .gate(in_1));
  Transistor transistor_3 (.in(1'b1), .out(out_2), .gate(transistor_1_out));
  Transistor #(.\type ("n")) transistor_4 (.in(1'b0), .out(out_2), .gate(transistor_1_out));
endmodule
